# Fritzing sketch Diagrama (saved by Fritzing 0.9.0b)
breadboards: 1

parts:
  Part1 = Arduino Uno (Rev3)
  J1 = Piezo Speaker
  R1 = Resistor [tolerance=±5% resistance=100 package=THT]

nets:
  N1: Part1.D8, R1.Pin_1
  N2: Part1.GND, J1.pin1
  N3: J1.pin2, R1.Pin_0
