# Fritzing sketch Diagrama_1 (saved by Fritzing 0.9.0b)
breadboards: 1

parts:
  Part1 = Arduino Uno (Rev3)
  LED1 = smd LED [color="Red (633nm)" package="0603 [SMD]"]
  R1 = Resistor [tolerance=±5% resistance=220 package=THT]
  S1 = Pushbutton [package="[THT]"]

nets:
  N1: Part1.D8, LED1.anode
  N2: Part1.GND, S1.Pin_3, S1.Pin_4
  N3: LED1.cathode, R1.Pin_1
  N4: R1.Pin_0, S1.Pin_1, S1.Pin_2
