# Fritzing sketch Diagrama (saved by Fritzing 0.9.0b)
breadboards: 1

parts:
  Part1 = Arduino Uno (Rev3)
  LCD1 = LCD screen
  R2 = Resistor [tolerance=±5% resistance=1k package=THT]
  R3 = Resistor [tolerance=±5% resistance=220 package=THT]
  R4 = Resistor [tolerance=±5% resistance=1k package=THT]
  R5 = Resistor [tolerance=±5% resistance=1k package=THT]
  Part2 = Thumb Joystick

nets:
  GND: Part1.A0, Part1.D12/MISO, Part1.GND, LCD1.VSS, LCD1.R/W, LCD1.LED-, R2.Pin_0, Part2.GND, Part2.SEL, Part2.HORZ
  N1: Part1.A1, Part2.VERT
  N2: Part1.D2, LCD1.RS
  N3: Part1.D3_PWM, LCD1.E
  N4: Part1.D4, LCD1.DB4
  N5: Part1.D5_PWM, LCD1.DB5
  N6: Part1.D6_PWM, LCD1.DB6
  N7: Part1.D7, LCD1.DB7
  5V: Part1.5V, LCD1.VDD, R3.Pin_1, Part2.VCC
  N8: LCD1.V0, R5.Pin_1
  N9: LCD1.LED+, R3.Pin_0
  N10: R2.Pin_1, R4.Pin_1
  N11: R4.Pin_0, R5.Pin_0

notes:
  Vcc = +5V
  VER = VRY
  HOR = VRX
  SEL = SW
