# Fritzing sketch Diagrama (saved by Fritzing 0.9.0b)
breadboards: 1

parts:
  Part1 = Arduino Uno (Rev3)
  LCD1 = LCD screen
  R2 = Resistor [tolerance=±5% resistance=1k package=THT]
  R3 = Resistor [tolerance=±5% resistance=220 package=THT]
  R4 = Resistor [tolerance=±5% resistance=1k package=THT]
  R5 = Resistor [tolerance=±5% resistance=1k package=THT]
  R6 = Resistor [tolerance=±5% resistance=220 package=THT]
  R7 = Resistor [tolerance=±5% resistance=220 package=THT]
  R8 = Resistor [tolerance=±5% resistance=220 package=THT]
  LED1 = RGB LED (com. cathode, rbg) [package="5 mm [THT]"]  # not connected

nets:
  N1: Part1.D9_PWM, R6.Pin_0
  N2: Part1.D10_PWM/SS, R7.Pin_0
  N3: Part1.D11_PWM/MOSI, R8.Pin_0
  GND: Part1.GND, LCD1.VSS, LCD1.R/W, LCD1.LED-, R2.Pin_0
  N4: Part1.D2, LCD1.RS
  N5: Part1.D3_PWM, LCD1.E
  N6: Part1.D4, LCD1.DB4
  N7: Part1.D5_PWM, LCD1.DB5
  N8: Part1.D6_PWM, LCD1.DB6
  N9: Part1.D7, LCD1.DB7
  5V: Part1.5V, LCD1.VDD, R3.Pin_1
  N10: LCD1.V0, R5.Pin_1
  N11: LCD1.LED+, R3.Pin_0
  N12: R2.Pin_1, R4.Pin_1
  N13: R4.Pin_0, R5.Pin_0
