# Fritzing sketch Diagrama (saved by Fritzing 0.9.0b)
breadboards: 1

parts:
  Part1 = Arduino Uno (Rev3)
  IR1 = TSOP312.., 314.. [package=THT]  # not connected
  LED1 = LED - 5mm [color="Red (633nm)" package="5 mm [THT]"]
  R1 = Resistor [tolerance=±5% resistance=10k package=THT]

nets:
  N1: Part1.D11_PWM/MOSI, R1.Pin_0
  N2: Part1.5V, LED1.anode
  N3: LED1.cathode, R1.Pin_1

notes:
  Sensor IR:
  Pin 1: leer valor
  Pin 2: gnd
  Pin 3: 5v
