# Fritzing sketch Diagrama (saved by Fritzing 0.9.0b)
breadboards: 1

parts:
  Part1 = Arduino Uno (Rev3)
  7_Segment1 = 7 Segment Display
  R1 = Resistor [tolerance=±5% resistance=220 package=THT]
  R2 = Resistor [tolerance=±5% resistance=220 package=THT]
  R3 = Resistor [tolerance=±5% resistance=220 package=THT]
  R4 = Resistor [tolerance=±5% resistance=220 package=THT]
  R5 = Resistor [tolerance=±5% resistance=220 package=THT]
  R6 = Resistor [tolerance=±5% resistance=220 package=THT]
  R7 = Resistor [tolerance=±5% resistance=220 package=THT]
  R8 = Resistor [tolerance=±5% resistance=220 package=THT]

nets:
  N1: Part1.D8, R7.Pin_1
  N2: Part1.D9_PWM, R8.Pin_1
  N3: Part1.D2, R1.Pin_1
  N4: Part1.D3_PWM, R2.Pin_1
  N5: Part1.D4, R3.Pin_1
  N6: Part1.D5_PWM, R4.Pin_1
  N7: Part1.D6_PWM, R5.Pin_1
  N8: Part1.D7, R6.Pin_1
  N9: Part1.5V, 7_Segment1.common_anode
  N10: 7_Segment1.Segment_E, R6.Pin_0
  N11: 7_Segment1.Segment_D, R5.Pin_0
  N12: 7_Segment1.Segment_C, R4.Pin_0
  N13: 7_Segment1.Segment_DP, R3.Pin_0
  N14: 7_Segment1.Segment_B, R2.Pin_0
  N15: 7_Segment1.Segment_A, R1.Pin_0
  N16: 7_Segment1.Segment_F, R8.Pin_0
  N17: 7_Segment1.Segment_G, R7.Pin_0
